# Fritzing sketch Catfeed (saved by Fritzing 0.9.3b)

parts:
  U1 = ESP8266 NodeMCU LoLin module
  J1 = Basic Servo  # not connected
  HC-SR04_Sensor_1 = HC-SR04 Ultrasonic Distance Sensor

nets:
  3V3: U1.3V3, HC-SR04_Sensor_1.VCC
  N1: U1.D7, HC-SR04_Sensor_1.TRIG
  N2: U1.D8, HC-SR04_Sensor_1.ECHO
  GND: U1.GND, HC-SR04_Sensor_1.GND

custom parts:
  ESP8266 NodeMCU LoLin module: ESP8266 based NodeMCU
